// Logisim project PipelinedProcessor.circ as structural Verilog: 2 circuits, main circuit main
module main (
);

  wire ALUSrc, clk, DisableIR, DisablePC, Ex_ALUSrc, Ex_signExtend, JumpOP, Mem_MemoryRead, Mem_MemoryWrite,
       MemoryRead, MemoryWrite, not_1_out, not_2_out, not_3_out, RegWrite, signExtend, SLT, WB_RegWrite,
       ZeroFlag;
  wire [1:0] BranchOP, Ex_MEMsignals, ExecutionSrc, F, ForwardA, ForwardB, MemorySrc, PCSrc, RegDest,
       RegisterWSrc, WB_RegDest, WB_RegisterWSrc;
  wire [2:0] Ex_Rd, ID_Rd, Mem_Rd, Rd, Rs, Rt, WB_Rd;
  wire [3:0] ALUop, Ex_ALUop;
  wire [4:0] Ex_Imm5, Ex_Opcode, Ex_WBsignals, Imm5, Mem_Opcode, Mem_WBsignals, Opcode;
  wire [10:0] Ex_Imm11, Imm11;
  wire [15:0] bit_extender_1_out, bit_extender_2_out, bit_extender_3_out, BranchPC, Ex_ALUout,
       Ex_ReturnAddress, Ex_Rs, Ex_Rt, Ex_ShiftedImm, extendedImmediate, ID_PC, ID_ReturnAdress, IR, JumpPC,
       Mem_ALUout, Mem_MemoryData, Mem_ReturnAddress, Mem_Rt, Mem_ShiftedImm, Mem_ShiftedImmediate,
       multiplexer_1_out, multiplexer_3_out, multiplexer_4_out, multiplexer_5_out, multiplexer_6_out,
       multiplexer_7_out, multiplexer_8_out, multiplexer_9_out, PC, PC_1, RegisterWrite, rom_1_data, RsValue,
       RtValue, WB_ALUout, WB_MemoryData, WB_ReturnAddress, WB_ShiftedImmediate;

  Multiplexer #(.select(2), .width(16), .enable("false")) multiplexer_1 (
    .in0({16{1'b0}}), .in1(BranchPC), .in2(JumpPC), .in3(PC_1), .out(multiplexer_1_out), .sel(PCSrc));
  // Probe on PCSrc
  Register #(.width(16)) register_1 (.D(multiplexer_1_out), .Q(PC), .clk(clk));  // open: en, clr
  Adder #(.width(16)) adder_1 (.a(16'h1), .b(PC), .out(PC_1), .cin(1'b0));  // open: cout
  ROM #(.addrWidth(16), .dataWidth(16)) rom_1 (.addr(PC), .data(rom_1_data), .sel(1'b1));
  not not_1 (not_1_out, DisablePC);
  Register #(.width(16)) PCRegister (.D(PC), .en(not_1_out), .Q(ID_PC), .clk(clk));  // open: clr
  Register #(.width(16)) ReturnAddress (.D(PC_1), .Q(ID_ReturnAdress), .clk(clk));  // open: en, clr
  Register #(.width(16)) InstructionRegister (.D(rom_1_data), .en(not_2_out), .Q(IR), .clk(clk));  // open: clr
  not not_2 (not_2_out, DisableIR);
  // JumpControl jumpcontrol_1: pin names not known; wires that end beside it: PC, RsValue, Imm11, JumpOP, JumpPC
  // Probe on Opcode
  InstructionSplitter instructionsplitter_1 (
    .Instruction(IR), .Op(Opcode), .F(F), .Rd(Rd), .Rs(Rs), .Rt(Rt), .Imm5(Imm5), .Imm11(Imm11));
  ControlUnit controlunit_1 (
    .Opcode(Opcode), .Function(F), .ALUop(ALUop), .ALUSrc(ALUSrc), .signExtend(signExtend),
    .RegWrite(RegWrite), .RegDest(RegDest), .RegWSrc(RegisterWSrc), .memoryRead(MemoryRead),
    .memoryWrite(MemoryWrite), .PCSrc(PCSrc), .BrachOP(BranchOP), .JumpOP(JumpOP));
  Clock clock_1 (.out(clk));
  // Probe on Rs
  // Probe on Rt
  // Probe on Rd
  // Probe on Imm5
  // Probe on BranchOP
  BranchControl branchcontrol_1 (
    .Operation(BranchOP), .Zero(ZeroFlag), .Less_Than(SLT), .Imm5(Imm5), .PC(PC), .newPC(BranchPC));
  Multiplexer #(.select(2), .width(3), .enable("false")) multiplexer_2 (
    .in0(Rt), .in1(Rd), .in2(3'b001), .in3(3'b111), .out(ID_Rd), .sel(WB_RegDest));
  // RegisterFile registerfile_1: pin names not known; wires that end beside it: Rs, Rt, WB_Rd, RsValue
  Multiplexer #(.select(2), .width(16), .enable("false")) multiplexer_3 (
    .in0(Mem_ALUout), .in1(Mem_ShiftedImm), .in2(Mem_ReturnAddress), .in3(Mem_MemoryData),
    .out(multiplexer_3_out), .sel(MemorySrc));
  Multiplexer #(.select(2), .width(16), .enable("false")) multiplexer_4 (
    .in0(Mem_ALUout), .in1(Mem_ShiftedImm), .in2(Mem_ReturnAddress), .in3(Mem_MemoryData),
    .out(multiplexer_4_out), .sel(MemorySrc));
  Multiplexer #(.select(2), .width(16), .enable("false")) multiplexer_5 (
    .in0(Ex_ALUout), .in1(Ex_ShiftedImm), .in2(Ex_ReturnAddress), .out(multiplexer_5_out), .sel(ExecutionSrc));  // open: in3
  Multiplexer #(.select(2), .width(16), .enable("false")) multiplexer_6 (
    .in0(Ex_ALUout), .in1(Ex_ShiftedImm), .in2(Ex_ReturnAddress), .out(multiplexer_6_out), .sel(ExecutionSrc));  // open: in3
  Multiplexer #(.select(2), .width(16), .enable("false")) multiplexer_7 (
    .in0(RsValue), .in1(multiplexer_5_out), .in2(multiplexer_3_out), .out(multiplexer_7_out), .sel(ForwardA));  // open: in3
  Multiplexer #(.select(2), .width(16), .enable("false")) multiplexer_8 (
    .in0(RtValue), .in1(multiplexer_6_out), .in2(multiplexer_4_out), .out(multiplexer_8_out), .sel(ForwardB));  // open: in3
  Register #(.width(16)) ReturnAddressRegister (.D(ID_ReturnAdress), .Q(Ex_ReturnAddress), .clk(clk));  // open: en, clr
  Register #(.width(11)) u_imm11 (.D(Imm11), .Q(Ex_Imm11), .clk(clk));  // open: en, clr
  Register #(.width(5)) u_imm5 (.D(Imm5), .Q(Ex_Imm5), .clk(clk));  // open: en, clr
  Register #(.width(16)) OperandA (.D(multiplexer_7_out), .Q(Ex_Rs), .clk(clk));  // open: en, clr
  Register #(.width(16)) OperandB (.D(multiplexer_8_out), .Q(Ex_Rt), .clk(clk));  // open: en, clr
  Register #(.width(3)) Rd2 (.D(ID_Rd), .Q(Ex_Rd), .clk(clk));  // open: en, clr
  Register #(.width(6)) ExecutionSignals (
    .D({signExtend, ALUSrc, ALUop}), .Q({Ex_signExtend, Ex_ALUSrc, Ex_ALUop}), .clk(clk));  // open: en, clr
  Register #(.width(5)) WriteBackSignals (
    .D({RegWrite, RegDest, RegisterWSrc}), .Q(Ex_WBsignals), .clk(clk));  // open: en, clr
  Register #(.width(2)) MemorySignals (.D({MemoryRead, MemoryWrite}), .Q(Ex_MEMsignals), .clk(clk));  // open: en, clr
  Register #(.width(5)) u_Opcode (.D(Opcode), .Q(Ex_Opcode), .clk(clk));  // open: en, clr
  assign bit_extender_1_out = {{11{1'b0}}, Ex_Imm5};  // Bit_Extender bit_extender_1
  assign bit_extender_2_out = {{11{Ex_Imm5[4]}}, Ex_Imm5};  // Bit_Extender bit_extender_2
  Multiplexer #(.width(16), .enable("false")) multiplexer_9 (
    .in0(Ex_Rt), .in1(extendedImmediate), .out(multiplexer_9_out), .sel(Ex_ALUSrc));
  assign extendedImmediate = not_3_out ? bit_extender_1_out : 16'bz;  // Controlled_Buffer controlled_buffer_1
  not not_3 (not_3_out, Ex_signExtend);
  assign extendedImmediate = Ex_signExtend ? bit_extender_2_out : 16'bz;  // Controlled_Buffer controlled_buffer_2
  assign bit_extender_3_out = {{5{1'b0}}, Ex_Imm11};  // Bit_Extender bit_extender_3
  Shifter #(.width(16)) shifter_1 (.in(bit_extender_3_out), .\dist (4'b0101), .out(Ex_ShiftedImm));
  ALU alu_1 (.in_1(Ex_ALUop), .in_2(Ex_Rs), .in_3(multiplexer_9_out), .out_6(Ex_ALUout));  // open: out_4, out_5
  Register #(.width(16)) RtValueRegister (.D(Ex_Rt), .Q(Mem_Rt), .clk(clk));  // open: en, clr
  Register #(.width(3)) Rd3 (.D(Ex_Rd), .Q(Mem_Rd), .clk(clk));  // open: en, clr
  Register #(.width(5)) WriteBackSignals_2 (.D(Ex_WBsignals), .Q(Mem_WBsignals), .clk(clk));  // open: en, clr
  Register #(.width(2)) MemorySignals_2 (
    .D(Ex_MEMsignals), .Q({Mem_MemoryRead, Mem_MemoryWrite}), .clk(clk));  // open: en, clr
  Register #(.width(16)) ALU_Output (.D(Ex_ALUout), .Q(Mem_ALUout), .clk(clk));  // open: en, clr
  Register #(.width(16)) Shifted_Immediate (.D(Ex_ShiftedImm), .Q(Mem_ShiftedImmediate), .clk(clk));  // open: en, clr
  Register #(.width(5)) Opcode_2 (.D(Ex_Opcode), .Q(Mem_Opcode), .clk(clk));  // open: en, clr
  Register #(.width(16)) ReturnAddressRegister_2 (
    .D(Ex_ReturnAddress), .Q(Mem_ReturnAddress), .clk(clk));  // open: en, clr
  Data_Memory data_memory_1 (
    .CLK(clk), .Memory_Enable(1'b1), .Memory_Read(Mem_MemoryRead), .Memory_Write(Mem_MemoryWrite),
    .Address(Mem_ALUout), .Data_In(Mem_Rt), .Data_Out(Mem_MemoryData));
  Register #(.width(16)) ReturnAddressRegister_3 (
    .D(Mem_ReturnAddress), .Q(WB_ReturnAddress), .clk(clk));  // open: en, clr
  Register #(.width(3)) Rd3_2 (.D(Mem_Rd), .Q(WB_Rd), .clk(clk));  // open: en, clr
  Register #(.width(5)) WriteBackSignals_3 (
    .D(Mem_WBsignals), .Q({WB_RegWrite, WB_RegDest, WB_RegisterWSrc}), .clk(clk));  // open: en, clr
  Register #(.width(16)) ALU_Output_2 (.D(Mem_ALUout), .Q(WB_ALUout), .clk(clk));  // open: en, clr
  Register #(.width(16)) Shifted_Immediate_2 (.D(Mem_ShiftedImm), .Q(WB_ShiftedImmediate), .clk(clk));  // open: en, clr
  Register #(.width(16)) Memory (.D(Mem_MemoryData), .Q(WB_MemoryData), .clk(clk));  // open: en, clr
  Multiplexer #(.select(2), .width(16), .enable("false")) multiplexer_10 (
    .in0(WB_ALUout), .in1(WB_MemoryData), .in2(WB_ShiftedImmediate), .in3(WB_ReturnAddress),
    .out(RegisterWrite), .sel(WB_RegisterWSrc));

  // Notes on the sheet:
  //   Instruction Fetch
  //   contents of rom_1 (hex, n*v repeats v):
  //   9000 280b 97ff 2fca 681a 840 880 8c0 6001 9808 9bc8 f000
  //   Instruction Decode
  //   Execution
  //   Memory
  //   Write Back
endmodule

module ForwardingSourceControl (
  input  OP4,
  input  OP3,
  input  OP2,
  input  OP1,
  input  OP0,
  output S1,
  output S0
);

  wire and_2_out, and_3_out, not_1_out, not_2_out;

  and and_1 (S1, OP3, OP2);
  not not_1 (not_1_out, OP1);
  not not_2 (not_2_out, OP3);
  and and_2 (and_2_out, OP3, OP2, not_1_out);
  and and_3 (and_3_out, OP4, not_2_out);
  or or_1 (S0, and_2_out, and_3_out);
endmodule
